# Fritzing sketch Version0.8.1 NEO-CYCLO (saved by Fritzing 0.9.3b)
breadboards: 1

parts:
  U1 = attiny85 [package=dip]
  SPKR1 = Loudspeaker
  C1 = Ceramic Capacitor [capacitance=100nF package="100 mil [THT, multilayer]"]
  Pot1 = Rotary Potentiometer (Small) [maximum_resistance=10kΩ package=THT]
  Pot2 = Rotary Potentiometer (Small) [maximum_resistance=10kΩ package=THT]
  C3 = Ceramic Capacitor [capacitance=100nF package="100 mil [THT, multilayer]"]
  neopixel1 = Neopixel Ring 12
  S1 = Toggle Switch [package=THT]
  TRS1 = Audio Jack (TRS) 3.5mm [package="4Ucon 08780 [THT]"]
  R3 = Resistor [tolerance=±5% resistance=10k package=THT]
  R4 = Resistor [tolerance=±5% resistance=10k package=THT]
  R5 = Resistor [tolerance=±5% resistance=100 package=THT]
  R6 = Resistor [tolerance=±5% resistance=10k package=THT]
  R7 = Resistor [tolerance=±5% resistance=10k package=THT]
  VCC1 = Battery
  C4 = Electrolytic Capacitor [capacitance=100µF package="100 mil [THT, electrolytic]"]
  LED1 = LED - 5mm [color="Red (633nm)" package="5 mm [THT]"]
  R8 = Resistor [tolerance=±5% resistance=1k package=THT]
  S2 = Pushbutton [package="[THT]"]
  S3 = Pushbutton [package="[THT]"]
  R9 = Resistor [tolerance=±5% resistance=10k package=THT]
  R10 = Resistor [tolerance=±5% resistance=4.7k package=THT]

nets:
  N1: U1.Pin_2, C1.1, R3.Pin_1, R4.Pin_0, R9.Pin_0, R10.Pin_0
  N2: U1.Pin_3, Pot2.wiper
  GND: U1.Pin_4, SPKR1.pin2, Pot1.leg1, Pot2.leg1, C3.0, neopixel1.GND, TRS1.Sleeve, R4.Pin_1, VCC1.-, LED1.cathode, S2.Pin_1, S2.Pin_2, S3.Pin_1, S3.Pin_2
  N3: U1.Pin_5, R5.Pin_0
  N4: U1.Pin_6, C4.+, R8.Pin_0
  N5: U1.Pin_7, Pot1.wiper
  3V/VCC: U1.Pin_8, C3.1, neopixel1.VCC, S1.L1, R3.Pin_0, R6.Pin_0, R7.Pin_0
  N6: SPKR1.pin1, C4.-
  N7: C1.0, TRS1.Ring
  N8: Pot1.leg2, R7.Pin_1
  N9: Pot2.leg2, R6.Pin_1
  N10: neopixel1.IN, R5.Pin_1
  N11: S1.COM, VCC1.+
  N12: LED1.anode, R8.Pin_1
  N13: S2.Pin_3, S2.Pin_4, R9.Pin_1
  N14: S3.Pin_3, S3.Pin_4, R10.Pin_1

notes:
  SoundProgInput
  NEO-Cyclo-Synth
  a variant of the Berliner Schule 2085
  Version 0.8 NEO
  100 Ohm Speaker

custom parts:
  Neopixel Ring 12: Neopixel Ring x12
