# Fritzing sketch Version0.8.1 NEO-CYCLO_BreadBoard (saved by Fritzing 0.9.3b)
stripboards: 1

parts:
  U1 = attiny85 [package=dip]
  SPKR1 = Loudspeaker
  C1 = Ceramic Capacitor [capacitance=100nF package="100 mil [THT, multilayer]"]
  C3 = Ceramic Capacitor [capacitance=100nF package="100 mil [THT, multilayer]"]
  S1 = Toggle Switch [package=THT]
  TRS1 = Audio Jack (TRS) 3.5mm [package="4Ucon 08780 [THT]"]
  R3 = Resistor [tolerance=±5% resistance=10k package=THT]
  R4 = Resistor [tolerance=±5% resistance=10k package=THT]
  R5 = Resistor [tolerance=±5% resistance=100 package=THT]
  R6 = Resistor [tolerance=±5% resistance=10k package=THT]
  R7 = Resistor [tolerance=±5% resistance=10k package=THT]
  VCC1 = Battery
  C4 = Electrolytic Capacitor [capacitance=100µF package="100 mil [THT, electrolytic]"]
  LED1 = LED - 5mm [color="Red (633nm)" package="5 mm [THT]"]
  R8 = Resistor [tolerance=±5% resistance=1k package=THT]
  S2 = Pushbutton [package="[THT]"]
  S3 = Pushbutton [package="[THT]"]
  R9 = Resistor [tolerance=±5% resistance=10k package=THT]
  R10 = Resistor [tolerance=±5% resistance=4.7k package=THT]
  R11 = Rotary Potentiometer (Large) [maximum_resistance=10kΩ package=THT]
  R12 = Rotary Potentiometer (Large) [maximum_resistance=10kΩ package=THT]
  neopixel1 = Neopixel Ring 12

nets:
  N1: U1.Pin_2, C1.1, R3.Pin_1, R4.Pin_0, R9.Pin_0, R10.Pin_0
  N2: U1.Pin_3, R12.wiper
  GND: U1.Pin_4, SPKR1.pin2, C3.0, TRS1.Sleeve, R4.Pin_1, VCC1.-, S2.Pin_1, S2.Pin_2, S3.Pin_1, S3.Pin_2, R11.leg2, R12.leg1, neopixel1.GND
  N3: U1.Pin_5, R5.Pin_0
  N4: U1.Pin_6, C4.+, R8.Pin_0
  N5: U1.Pin_7, R11.wiper
  VCC: U1.Pin_8, C3.1, S1.L1, R3.Pin_0, R6.Pin_0, R7.Pin_0, LED1.anode, neopixel1.VCC
  N6: SPKR1.pin1, C4.-
  N7: C1.0, TRS1.Ring
  N8: S1.COM, VCC1.+
  N9: R5.Pin_1, neopixel1.IN
  N10: R6.Pin_1, R12.leg2
  N11: R7.Pin_1, R11.leg1
  N12: LED1.cathode, R8.Pin_1
  N13: S2.Pin_3, S2.Pin_4, R9.Pin_1
  N14: S3.Pin_3, S3.Pin_4, R10.Pin_1

notes:
  SoundProgInput
  NEO-Cyclo-Synth
  a variant of the Berliner Schule 2085
  Version 0.8 NEO
  100 Ohm Speaker

custom parts:
  Neopixel Ring 12: Neopixel Ring x12
